# Fritzing sketch LED-Schalter (saved by Fritzing 0.9.4)
breadboards: 1

parts:
  Raspberry_Pi_1 = Raspberry Pi 3 [part_number=RPI-3-V1.2]
  LED_1_6_V = LED - 5mm [color="Red (633nm)" current=10mA package="5 mm [THT]"]
  R1 = Resistor [tolerance=±1% resistance=220 package="1206 [SMD]"]
  S1 = Pushbutton [package="[THT]"]
  R2 = Resistor [tolerance=±5% resistance=220 package=THT]

nets:
  N1: Raspberry_Pi_1.3v3, S1.Pin_1, S1.Pin_2
  N2: Raspberry_Pi_1.GPIO24, S1.Pin_3, S1.Pin_4, R2.Pin_0
  N3: Raspberry_Pi_1.GPIO18, LED_1_6_V.anode
  N4: Raspberry_Pi_1.GND, R1.Pin_0, R2.Pin_1
  N5: LED_1_6_V.cathode, R1.Pin_1
