# Fritzing sketch Temperatur_messen (saved by Fritzing 0.9.4)
breadboards: 1

parts:
  Raspberry_Pi_1 = Raspberry Pi 3 [part_number=RPI-3-V1.2]
  DS1 = DS18B20 1-Wire Temperature Sensor [part_number=DS18B20]
  R1 = Resistor [tolerance=±5% resistance=220 package=THT]

nets:
  N1: Raspberry_Pi_1.GPIO4, DS1.DQ, R1.Pin_0
  GND: Raspberry_Pi_1.GND, DS1.GND
  N2: DS1.VDD, R1.Pin_1
